# Fritzing sketch esp_serial_comms (saved by Fritzing 1.0.5)
breadboards: 2

parts:
  Part1 = Adafruit ESP32 Feather V2
  Part2 = Adafruit ESP32 Feather V2

nets:
  N1: Part1.V_NEOI2C, Part1.SCL
  N2: Part2.V_NEOI2C, Part2.SCL
