# Fritzing sketch esp_intro (saved by Fritzing 1.0.5)
breadboards: 1

parts:
  S2 = Pushbutton [package=THT]  # not connected
  R3 = Resistor [tolerance=±5% power=0.25W resistance=10k package=THT]
  LED2 = LED - 5mm [color="Green (560nm)" current=0.030A package="5 mm [THT]"]
  Part1 = Adafruit ESP32 Feather V2

nets:
  N1: R3.Pin_1, LED2.anode
  N2: Part1.V_NEOI2C, Part1.SCL
